// Logisim project TheLife.circ as structural Verilog: 6 circuits, main circuit main
module main (
);

  wire [14:0] show_module_1_out_1, show_module_1_out_2, show_module_1_out_3, show_module_1_out_4,
       show_module_1_out_5, show_module_1_out_6, show_module_1_out_7, show_module_1_out_8,
       show_module_1_out_9, show_module_1_out_10, show_module_1_out_11, show_module_1_out_12,
       show_module_1_out_13, show_module_1_out_14, show_module_1_out_15;

  DotMatrix #(.matrixcols(15), .matrixrows(15)) dotmatrix_1 (
    .col0(show_module_1_out_1), .col1(show_module_1_out_2), .col2(show_module_1_out_3),
    .col3(show_module_1_out_4), .col4(show_module_1_out_5), .col5(show_module_1_out_6),
    .col6(show_module_1_out_7), .col7(show_module_1_out_8), .col8(show_module_1_out_9),
    .col9(show_module_1_out_10), .col10(show_module_1_out_11), .col11(show_module_1_out_12),
    .col12(show_module_1_out_13), .col13(show_module_1_out_14), .col14(show_module_1_out_15));
  Show_module show_module_1 (
    .out_1(show_module_1_out_1), .out_2(show_module_1_out_2), .out_3(show_module_1_out_3),
    .out_4(show_module_1_out_4), .out_5(show_module_1_out_5), .out_6(show_module_1_out_6),
    .out_7(show_module_1_out_7), .out_8(show_module_1_out_8), .out_9(show_module_1_out_9),
    .out_10(show_module_1_out_10), .out_11(show_module_1_out_11), .out_12(show_module_1_out_12),
    .out_13(show_module_1_out_13), .out_14(show_module_1_out_14), .out_15(show_module_1_out_15));
endmodule

module Show_module (
  output [14:0] out_1,
  output [14:0] out_2,
  output [14:0] out_3,
  output [14:0] out_4,
  output [14:0] out_5,
  output [14:0] out_6,
  output [14:0] out_7,
  output [14:0] out_8,
  output [14:0] out_9,
  output [14:0] out_10,
  output [14:0] out_11,
  output [14:0] out_12,
  output [14:0] out_13,
  output [14:0] out_14,
  output [14:0] out_15
);
endmodule

module Cell (
  input  upper_center,
  input  upper_left,
  input  upper_right,
  input  left,
  input  right,
  input  bottom_left,
  input  bottom_right,
  input  bottom_center,
  input  tick,
  input  waspressed,
  output State
);

  State_manager state_manager_1 (
    .nb1(upper_center), .nb2(upper_left), .nb3(upper_right), .nb4(left), .nb5(right), .nb6(bottom_left),
    .nb7(bottom_right), .nb8(bottom_center), .user_s_hand(tick), .tick(waspressed), .State(State));
endmodule

module State_manager (
  input  nb1,
  input  nb2,
  input  nb3,
  input  nb4,
  input  nb5,
  input  nb6,
  input  nb7,
  input  nb8,
  input  user_s_hand,
  input  tick,
  output State
);

  wire and_1_out, and_2_out, and_3_out, and_4_out, not_1_out, not_2_out, not_3_out, not_4_out, or_1_out,
       or_2_out, or_3_out;
  wire [1:0] adder_1_out, adder_2_out, adder_3_out, adder_4_out, adder_5_out, adder_6_out;
  wire [2:0] adder_7_out;
  wire [2:2] adder_5_cout, adder_6_cout;

  Adder #(.width(1)) adder_1 (.a(nb1), .b(nb2), .out(adder_1_out[0]), .cout(adder_1_out[1]));  // open: cin
  Adder #(.width(1)) adder_2 (.a(nb3), .b(nb4), .out(adder_2_out[0]), .cout(adder_2_out[1]));  // open: cin
  Adder #(.width(1)) adder_3 (.a(nb5), .b(nb6), .out(adder_3_out[0]), .cout(adder_3_out[1]));  // open: cin
  Adder #(.width(1)) adder_4 (.a(nb7), .b(nb8), .out(adder_4_out[0]), .cout(adder_4_out[1]));  // open: cin
  Adder #(.width(2)) adder_5 (
    .a(adder_1_out), .b(adder_2_out), .out(adder_5_out), .cout(adder_5_cout[2]));  // open: cin
  Adder #(.width(2)) adder_6 (
    .a(adder_3_out), .b(adder_4_out), .out(adder_6_out), .cout(adder_6_cout[2]));  // open: cin
  Adder #(.width(3)) adder_7 (
    .a({adder_5_cout[2], adder_5_out}), .b({adder_6_cout[2], adder_6_out}), .out(adder_7_out));  // open: cin, cout
  not not_1 (not_1_out, adder_7_out[2]);
  not not_2 (not_2_out, adder_7_out[0]);
  and and_1 (and_1_out, adder_7_out[0], adder_7_out[1], not_1_out);
  and and_2 (and_2_out, not_1_out, adder_7_out[1], not_2_out);
  or or_1 (or_1_out, user_s_hand, tick);
  not not_3 (not_3_out, user_s_hand);
  or or_2 (or_2_out, and_1_out, and_2_out);
  not not_4 (not_4_out, State);
  and and_3 (and_3_out, or_2_out, not_3_out);
  and and_4 (and_4_out, user_s_hand, not_4_out);
  or or_3 (or_3_out, and_3_out, and_4_out);
  Register #(.width(1), .trigger("falling")) register_1 (.D(or_3_out), .Q(State), .clk(or_1_out));  // open: en, clr

  // Notes on the sheet:
  //   3 живые
  //   2 живые
  //   Команда на смену состояния
  //   Оживание по правилам + нет команд от юзера
  //   Отрицание для смены состояния
endmodule

module Displaying_cells (
);

  Cell cell_1 ();  // open: upper_center, upper_left, upper_right, left, right, bottom_left, bottom_right, bottom_center, tick, waspressed, State
endmodule

module Row_of_cells (
  input  upper_1,
  input  upper_2,
  input  upper_3,
  input  upper_4,
  input  upper_5,
  input  upper_6,
  input  upper_7,
  input  upper_8,
  input  upper_9,
  input  upper_10,
  input  upper_11,
  input  upper_12,
  input  upper_13,
  input  upper_14,
  input  upper_15
);

  wire cell_1_state, cell_2_state, cell_3_state, cell_4_state, cell_5_state, cell_7_state, cell_9_state,
       cell_11_state, cell_13_state, cell_15_state;

  Cell cell_1 (
    .upper_center(upper_1), .upper_left(upper_15), .upper_right(upper_2), .left(cell_4_state),
    .right(cell_3_state), .State(cell_1_state));  // open: bottom_left, bottom_right, bottom_center, tick, waspressed
  Cell cell_2 (
    .upper_center(upper_9), .upper_left(upper_8), .upper_right(upper_10), .left(cell_15_state),
    .right(cell_4_state), .State(cell_2_state));  // open: bottom_left, bottom_right, bottom_center, tick, waspressed
  Cell cell_3 (
    .upper_center(upper_2), .upper_left(upper_1), .upper_right(upper_3), .right(cell_5_state),
    .State(cell_3_state));  // open: left, bottom_left, bottom_right, bottom_center, tick, waspressed
  Cell cell_4 (
    .upper_center(upper_10), .upper_left(upper_9), .upper_right(upper_11), .right(cell_4_state),
    .State(cell_4_state));  // open: left, bottom_left, bottom_right, bottom_center, tick, waspressed
  Cell cell_5 (
    .upper_center(upper_3), .upper_left(upper_2), .upper_right(upper_4), .right(cell_7_state),
    .State(cell_5_state));  // open: left, bottom_left, bottom_right, bottom_center, tick, waspressed
  Cell cell_6 (
    .upper_center(upper_11), .upper_left(upper_10), .upper_right(upper_12), .right(cell_4_state),
    .State(cell_4_state));  // open: left, bottom_left, bottom_right, bottom_center, tick, waspressed
  Cell cell_7 (
    .upper_center(upper_4), .upper_left(upper_3), .upper_right(upper_5), .right(cell_9_state),
    .State(cell_7_state));  // open: left, bottom_left, bottom_right, bottom_center, tick, waspressed
  Cell cell_8 (
    .upper_center(upper_12), .upper_left(upper_11), .upper_right(upper_13), .right(cell_4_state),
    .State(cell_4_state));  // open: left, bottom_left, bottom_right, bottom_center, tick, waspressed
  Cell cell_9 (
    .upper_center(upper_5), .upper_left(upper_4), .upper_right(upper_6), .right(cell_11_state),
    .State(cell_9_state));  // open: left, bottom_left, bottom_right, bottom_center, tick, waspressed
  Cell cell_10 (
    .upper_center(upper_13), .upper_left(upper_12), .upper_right(upper_14), .right(cell_4_state),
    .State(cell_4_state));  // open: left, bottom_left, bottom_right, bottom_center, tick, waspressed
  Cell cell_11 (
    .upper_center(upper_6), .upper_left(upper_5), .upper_right(upper_7), .right(cell_13_state),
    .State(cell_11_state));  // open: left, bottom_left, bottom_right, bottom_center, tick, waspressed
  Cell cell_12 (
    .upper_center(upper_14), .upper_left(upper_13), .upper_right(upper_15), .right(cell_4_state),
    .State(cell_4_state));  // open: left, bottom_left, bottom_right, bottom_center, tick, waspressed
  Cell cell_13 (
    .upper_center(upper_7), .upper_left(upper_6), .upper_right(upper_8), .right(cell_15_state),
    .State(cell_13_state));  // open: left, bottom_left, bottom_right, bottom_center, tick, waspressed
  Cell cell_14 (
    .upper_center(upper_15), .upper_left(upper_14), .upper_right(upper_1), .right(cell_1_state),
    .State(cell_4_state));  // open: left, bottom_left, bottom_right, bottom_center, tick, waspressed
  Cell cell_15 (
    .upper_center(upper_8), .upper_left(upper_7), .upper_right(upper_9), .right(cell_2_state),
    .State(cell_15_state));  // open: left, bottom_left, bottom_right, bottom_center, tick, waspressed
endmodule
